# Fritzing sketch customer_sketch (saved by Fritzing 1.0.0rc)
breadboards: 1

parts:
  LED1 = LED - 5mm [color="Green (565nm)" current=0.030A package="5 mm [THT]"]
  S1 = Pushbutton [package="[THT]"]
  R1 = Resistor [tolerance=±5% power=0.25W resistance=220 package=THT]
  S2 = Pushbutton [package="[THT]"]
  R2 = Resistor [tolerance=±5% power=0.25W resistance=220 package=THT]
  S3 = Pushbutton [package="[THT]"]
  R3 = Resistor [tolerance=±5% power=0.25W resistance=220 package=THT]

nets:
  N1: LED1.cathode, R1.Pin_0, R2.Pin_0, R3.Pin_0
  N2: S1.Pin_1, S1.Pin_2, R1.Pin_1
  N3: S1.Pin_3, S1.Pin_4, S2.Pin_3, S2.Pin_4, S3.Pin_3, S3.Pin_4
  N4: S2.Pin_1, S2.Pin_2, R2.Pin_1
  N5: S3.Pin_1, S3.Pin_2, R3.Pin_1

notes:
  Put ESP32 here.
  5
  10
  9
  6
  3V
  GND
