# Fritzing sketch tiago_sketch (saved by Fritzing 1.0.0rc)
breadboards: 1

parts:
  LED1 = LED - 5mm [color="Green (565nm)" current=0.030A package="5 mm [THT]"]
  LED2 = LED - 5mm [color="Yellow (595nm)" current=0.030A package="5 mm [THT]"]
  LED3 = LED - 5mm [color="Red (633nm)" current=0.030A package="5 mm [THT]"]
  LED4 = LED - 5mm [color="Blue (470nm)" current=0.030A package="5 mm [THT]"]
  S1 = Pushbutton [package="[THT]"]
  R1 = Resistor [tolerance=±5% power=0.25W resistance=220 package=THT]

nets:
  N1: LED1.cathode, LED2.cathode, LED3.cathode, LED4.cathode, R1.Pin_0
  N2: S1.Pin_1, S1.Pin_2, R1.Pin_1
  N3: S1.Pin_3, S1.Pin_4

notes:
  Put ESP32 here.
  12
  11
  10
  9
  8
  3V
  GND
