# Fritzing sketch smart-bin (saved by Fritzing 1.0.0rc)
breadboards: 1

parts:
  元件1 = Adafruit ESP32-S3 Feather [part_number="Adafruit #5323"]
  J1 = Basic Servo
  Компонент1 = Adafruit VL530X Time of Flight Distance Sensor [part_number="Adafruit #3317"]
  HC-SR04_Sensor_1 = HC-SR04 Ultrasonic Distance Sensor
  S1 = Momentary Switch [package=ksa_sealed_tac_switch]

nets:
  GND: 元件1.GND, 元件1.A2, J1.gnd, Компонент1.GND, HC-SR04_Sensor_1.GND, S1.3, S1.4
  N1: 元件1.SDA, Компонент1.SDA
  N2: 元件1.SCL, Компонент1.SCL
  VCC: 元件1.VBUS, J1.vcc, Компонент1.VCC, HC-SR04_Sensor_1.VCC
  N3: 元件1.D13, J1.pulse
  N4: 元件1.D12, HC-SR04_Sensor_1.ECHO
  N5: 元件1.D11, HC-SR04_Sensor_1.TRIG
  N6: S1.1, S1.2

custom parts:
  Adafruit ESP32-S3 Feather: The ESP32-S3 has arrived in Feather format - and what a great way to get started with this powerful new chip from Espressif! With dual 240 MHz cores, WiFi and BLE support, and native USB, this Feather is great for powering your IoT projects. That's right - it's the new Adafruit ESP32-S3 Feather! With native USB and 8 MB flash, this board will let you upgrade your existing ESP32 projects.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
  Adafruit VL530X Time of Flight Distance Sensor: The VL53L0X is a Time of Flight distance sensor like no other you've used! The sensor contains a very tiny invisible laser source, and a matching sensor. The VL53L0X can detect the "time of flight", or how long the light has taken to bounce back to the sensor. Since it uses a very narrow light source, it is good for determining distance of only the surface directly in front of it. Unlike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
