# Fritzing sketch circuit (saved by Fritzing 1.0.6)
breadboards: 1

parts:
  Adafruit_Feather_ESP32-C1 = Adafruit Feather ESP32-C6 [mn=Adafruit mpn=#5933 part_number=#5933]
  VCC1 = 4 x AAA Battery Mount [internal_resistance=0.1Ω]
  VCC2 = 4 x AAA Battery Mount [internal_resistance=0.1Ω]
  M1 = 1 chan 5v relay module
  M3 = DC Motor [voltage_(max)=6V voltage_(min)=3V]
  M4 = DC Motor [voltage_(max)=6V voltage_(min)=3V]

nets:
  N1: Adafruit_Feather_ESP32-C1.GND, VCC1.-, M1.pin_2
  N2: Adafruit_Feather_ESP32-C1.VBAT, VCC1.+, M1.pin_1
  N3: Adafruit_Feather_ESP32-C1.IO14, M1.pin_3
  N4: VCC2.-, M3.pin_1, M4.pin_1
  N5: VCC2.+, M1.pin_5
  N6: M1.pin_4, M3.pin_2, M4.pin_2

custom parts:
  1 chan 5v relay module: 1 Channel 5V Relay Module Board Shield with Optocoupler Support High and Low Level Trigger for Arduino.
